# Fritzing sketch Circuit (saved by Fritzing 0.9.4)
breadboards: 1

parts:
  Raspberry_Pi_1 = Raspberry Pi 3 [part_number=RPI-3-V1.2]
  VCC1 = 4 x AAA Battery Mount
  Part1 = Solid State High Level Relay Module [package=relay]
  M1 = DC Motor

nets:
  N1: Raspberry_Pi_1.GPIO3, Part1.CH1
  N2: Raspberry_Pi_1.GND, Part1.DC-
  N3: Raspberry_Pi_1.5V, Part1.DC+
  N4: VCC1.-, Part1.A1
  N5: Part1.B1, M1.pin_2

notes:
  5v relay module

custom parts:
  Solid State High Level Relay Module: 5V Omron solid state relay 240V 2A output with resistance fuse.
